# Fritzing sketch plant-watering-system (saved by Fritzing 0.9.3b)
breadboards: 1

parts:
  MH-ET_Live_Minikit_for_ESP1 = MH-ET Live Minikit for ESP32
  KY-1 = Relay [package=THT]
  Part1 = Soil Moisture Sensor
  M1 = DC Motor
  Power_plug1 = Power plug  # not connected
  Power_plug2 = Power plug

nets:
  N1: MH-ET_Live_Minikit_for_ESP1.IO34, Part1.SIG
  N2: MH-ET_Live_Minikit_for_ESP1.IO18, KY-1.in
  GND: MH-ET_Live_Minikit_for_ESP1.GND, KY-1.ground, Part1.GND
  VCC: MH-ET_Live_Minikit_for_ESP1.VCC, KY-1.power, Part1.VCC
  N3: KY-1.NO, M1.pin_1
  N4: M1.pin_2, Power_plug2.GND

notes:
  Plant
  Water
  6V
  water pump (6V)

custom parts:
  MH-ET Live Minikit for ESP32: MH-ET Live Minikit for ESP32 ( http://mh.nodebb.com/topic/8/mh-et-live-minikit-for-esp32/2/) PCB footprint is invalid.
  Relay: The Keyes 5V relay module is suitable for SCM development, home appliance control. It uses a 5V~12V TIL control signal which can control DC / AC signal.
