# Fritzing sketch plant-watering-system (saved by Fritzing 0.9.3b)

parts:
  Part1 = Soil Moisture Sensor
  M1 = DC Motor
  Power_plug2 = Power plug
  WeMos_D1_Mini1 = WeMos D1 Mini  # not connected
  WeMos_D1_Mini_Relay_Shield_V1 = WeMos D1 Mini Relay Shield V2  # not connected
  WeMos_D1_Mini_Protoboard_Shield1 = WeMos D1 Mini Protoboard Shield
  WeMos_D1_Mini_Dual_Base_Shield1 = WeMos D1 Mini Dual Base Shield  # not connected

nets:
  GND: Part1.GND, M1.pin_2, Power_plug2.GND, WeMos_D1_Mini_Protoboard_Shield1.G, WeMos_D1_Mini_Protoboard_Shield1.X7-Y7
  N1: Part1.SIG, WeMos_D1_Mini_Protoboard_Shield1.A0, WeMos_D1_Mini_Protoboard_Shield1.X2-Y2
  VCC: Part1.VCC, WeMos_D1_Mini_Protoboard_Shield1.3V3, WeMos_D1_Mini_Protoboard_Shield1.X2-Y8
  VCC_2: Power_plug2.VCC, WeMos_D1_Mini_Protoboard_Shield1.5V

notes:
  Plant
  Water
  5V
  water pump
  The Wemos is powered from the main power supply. However, when programming it via USB you need to disconnect that power supply.
  Wemos shields are stacked on a Wemos dual base shield.
